// Logisim project CLA.circ as structural Verilog: 7 circuits, main circuit CLA4
module CLA4 (
  input  Cin,
  input  [3:0] A,
  input  [3:0] B,
  output [3:0] S,
  output Cout,
  output V
);

  wire [3:0] carry4_1_ci, pg4_1_g, pg4_1_p;

  PG4 pg4_1 (.A(A), .B(B), .P(pg4_1_p), .G(pg4_1_g));
  Carry4 carry4_1 (.C0(Cin), .P(pg4_1_p), .G(pg4_1_g), .Ci(carry4_1_ci), .Cout(Cout), .V(V));
  assign S = pg4_1_p ^ carry4_1_ci;  // XOR_Gate xor_1, 4 bits wide

  // Notes on the sheet:
  //   overflow detection
endmodule

module PG1 (
  input  A,
  input  B,
  output P,
  output G
);

  xor xor_1 (P, A, B);
  and and_1 (G, A, B);
endmodule

module PG4 (
  input  [3:0] A,
  input  [3:0] B,
  output [3:0] P,
  output [3:0] G
);

  PG1 pg1_1 (.A(A[0]), .B(B[0]), .P(P[0]), .G(G[0]));
  PG1 pg1_2 (.A(A[1]), .B(B[1]), .P(P[1]), .G(G[1]));
  PG1 pg1_3 (.A(A[2]), .B(B[2]), .P(P[2]), .G(G[2]));
  PG1 pg1_4 (.A(A[3]), .B(B[3]), .P(P[3]), .G(G[3]));
endmodule

module Carry4 (
  input  C0,
  input  [3:0] P,
  input  [3:0] G,
  output [3:0] Ci,
  output Cout,
  output V
);

  wire and_1_out, and_2_out, and_3_out, and_4_out, and_5_out, and_6_out, and_7_out, and_8_out, and_9_out,
       and_10_out;

  and and_1 (and_1_out, P[0], C0);
  and and_2 (and_2_out, P[1], G[0]);
  and and_3 (and_3_out, P[1], P[0], C0);
  and and_4 (and_4_out, P[2], G[1]);
  and and_5 (and_5_out, P[2], P[1], G[0]);
  and and_6 (and_6_out, P[2], P[1], P[0], C0);
  and and_7 (and_7_out, P[3], G[2]);
  and and_8 (and_8_out, P[3], P[2], G[1]);
  and and_9 (and_9_out, P[3], P[2], P[1], G[0]);
  and and_10 (and_10_out, P[3], P[2], P[1], P[0], C0);
  or or_1 (Ci[1], G[0], and_1_out);
  or or_2 (Ci[2], G[1], and_2_out, and_3_out);
  or or_3 (Ci[3], G[2], and_4_out, and_5_out, and_6_out);
  or or_4 (Cout, G[3], and_7_out, and_8_out, and_9_out, and_10_out);
  xor xor_1 (V, Cout, Ci[3]);

  assign Ci[0] = C0;

  // Notes on the sheet:
  //   overflow detection
endmodule

module CLA16 (
  input  [15:0] B,
  input  [15:0] A,
  input  Cin,
  output V,
  output Cout,
  output [15:0] S
);

  wire cla4_1_cout, cla4_2_cout, cla4_3_cout;

  CLA4 cla4_1 (.B(B[3:0]), .S(S[3:0]), .A(A[3:0]), .Cin(Cin), .Cout(cla4_1_cout));  // open: V
  CLA4 cla4_2 (.B(B[7:4]), .S(S[7:4]), .A(A[7:4]), .Cin(cla4_1_cout), .Cout(cla4_2_cout));  // open: V
  CLA4 cla4_3 (.B(B[11:8]), .S(S[11:8]), .A(A[11:8]), .Cin(cla4_2_cout), .Cout(cla4_3_cout));  // open: V
  CLA4 cla4_4 (.B(B[15:12]), .V(V), .S(S[15:12]), .A(A[15:12]), .Cin(cla4_3_cout), .Cout(Cout));
endmodule

module CLA32 (
  input  [31:0] B,
  input  [31:0] A,
  input  Cin,
  output V,
  output [31:0] C
);

  wire cla16_1_cout;

  CLA16 cla16_1 (.Cin(Cin), .S(C[15:0]), .A(B[15:0]), .B(A[15:0]), .Cout(cla16_1_cout));  // open: V
  CLA16 cla16_2 (.Cin(cla16_1_cout), .S(C[31:16]), .V(V), .A(B[31:16]), .B(A[31:16]));  // open: Cout
endmodule

module CLA32_addsub (
  input  [31:0] A,
  input  [31:0] B,
  input  [3:0] Op,
  output V,
  output [31:0] C
);

  wire cla32_1_v, turnOn;
  wire [31:0] bit_extender_1_out, bit_extender_2_out, cla32_1_c, xor_1_out;

  assign bit_extender_1_out = {{31{Op[2]}}, Op[2]};  // Bit_Extender bit_extender_1
  assign xor_1_out = B ^ bit_extender_1_out;  // XOR_Gate xor_1, 32 bits wide
  and and_1 (turnOn, Op[1], ~Op[3]);  // AND_Gate
  assign bit_extender_2_out = {{31{turnOn}}, turnOn};  // Bit_Extender bit_extender_2
  CLA32 cla32_1 (.V(cla32_1_v), .C(cla32_1_c), .Cin(Op[2]), .B(xor_1_out), .A(A));
  assign C = cla32_1_c & bit_extender_2_out;  // AND_Gate and_2, 32 bits wide
  and and_3 (V, turnOn, cla32_1_v);

  // Notes on the sheet:
  //   Op2 == 1? subtract: add
  //   Op3 == 0 and Op1= = 1
  //   check active
  //   Arithmetic Operator
  //   If not arithmetic operator => V = 0
  //   Overflow
endmodule
